# Fritzing sketch Wiring_Diagram_Final (saved by Fritzing 0.9.3b)
breadboards: 1

parts:
  Part1 = Arduino Uno (Rev3)
  LED1 = smd LED [color="Red (633nm)" package="0603 [SMD]"]
  LED2 = smd LED [color="Green (555nm)" package="0603 [SMD]"]
  R1 = Resistor [tolerance=±5% resistance=220 package="1206 [SMD]"]
  R2 = Resistor [tolerance=±5% resistance=220 package="1206 [SMD]"]
  L1 = Solenoid
  R3 = Resistor [tolerance=±5% resistance=4.7k package="1206 [SMD]"]
  Q1 = Basic FET N-Channel [package="TO220 [THT]"]
  D1 = Diode [package=diode-1n4148]

nets:
  N1: Part1.D3_PWM, R3.Pin_1
  N2: Part1.D6_PWM, R2.Pin_1
  N3: Part1.D7, R1.Pin_1
  N4: Part1.GND, LED1.cathode, LED2.cathode, Q1.source
  N5: Part1.VIN, L1.pin1, D1.C
  N6: LED1.anode, R1.Pin_0
  N7: LED2.anode, R2.Pin_0
  N8: L1.pin2, Q1.drain, D1.A
  N9: R3.Pin_0, Q1.gate
